# Fritzing sketch ESPFernbedienungFritzing (saved by Fritzing 0.9.3b)
breadboards: 1

parts:
  Bauteil1 = Arduino Fio (Funnel I/O)
  LED1 = smd LED [color="Infrared (940nm)" package="0603 [SMD]"]
  R1 = Resistor [tolerance=±5% resistance=20 package=THT]
  R2 = Resistor [tolerance=±5% resistance=220 package=THT]
  IR1 = TSOP312.., 314.. [package=THT]
  Q1 = NPN-Transistor [package="TO92 [THT]"]

nets:
  N1: Bauteil1.VCC, Bauteil1.D0/RXI, LED1.anode, IR1.Vs
  GND: Bauteil1.GND, Bauteil1.D2, IR1.GND, Q1.E
  N2: Bauteil1.D3_PWM, R2.Pin_0
  N3: Bauteil1.D4, Bauteil1.D5_PWM, IR1.Data
  N4: LED1.cathode, R1.Pin_1
  N5: R1.Pin_0, Q1.C
  N6: R2.Pin_1, Q1.B
